// Logisim project lab3.circ as structural Verilog
module one_bit_adder (
  input  A,
  input  B,
  input  C_In,
  output Sum,
  output C_Out
);

  wire and_1_out, and_2_out, xor_1_out;

  xor xor_1 (xor_1_out, A, B);
  and and_1 (and_1_out, xor_1_out, C_In);
  and and_2 (and_2_out, A, B);
  xor xor_2 (Sum, xor_1_out, C_In);
  or or_1 (C_Out, and_1_out, and_2_out);
endmodule

module one_bit_ALU (
  input  [3:0] ALU_Ctrl,
  input  A,
  input  B,
  input  C_In,
  output R,
  output C_Out
);

  wire and_1_out, multiplexer_1_out, not_1_out, one_bit_adder_1_sum, or_1_out, xor_1_out;

  not not_1 (not_1_out, B);
  Multiplexer #(.enable("false")) multiplexer_1 (.in0(B), .in1(not_1_out), .out(multiplexer_1_out), .sel(ALU_Ctrl[2]));
  and and_1 (and_1_out, A, multiplexer_1_out);
  or or_1 (or_1_out, A, multiplexer_1_out);
  xor xor_1 (xor_1_out, A, multiplexer_1_out);
  one_bit_adder one_bit_adder_1 (.A(A), .B(multiplexer_1_out), .C_In(C_In), .Sum(one_bit_adder_1_sum), .C_Out(C_Out));
  Multiplexer #(.enable("false"), .select(2)) multiplexer_2 (
    .in0(and_1_out), .in1(or_1_out), .in2(xor_1_out), .in3(one_bit_adder_1_sum), .out(R), .sel(ALU_Ctrl[1:0]));
endmodule

module ALU4 (
  input  [3:0] ALU_Ctrl,
  input  C_In,
  input  [3:0] A,
  input  [3:0] B,
  output [3:0] R,
  output C_Out
);

  wire one_bit_alu_1_c_out, one_bit_alu_2_c_out, one_bit_alu_3_c_out;

  one_bit_ALU one_bit_alu_1 (
    .ALU_Ctrl(ALU_Ctrl), .A(A[0]), .B(B[0]), .C_In(C_In), .R(R[0]), .C_Out(one_bit_alu_1_c_out));
  one_bit_ALU one_bit_alu_2 (
    .ALU_Ctrl(ALU_Ctrl), .A(A[1]), .B(B[1]), .C_In(one_bit_alu_1_c_out), .R(R[1]), .C_Out(one_bit_alu_2_c_out));
  one_bit_ALU one_bit_alu_3 (
    .ALU_Ctrl(ALU_Ctrl), .A(A[2]), .B(B[2]), .C_In(one_bit_alu_2_c_out), .R(R[2]), .C_Out(one_bit_alu_3_c_out));
  one_bit_ALU one_bit_alu_4 (
    .ALU_Ctrl(ALU_Ctrl), .A(A[3]), .B(B[3]), .C_In(one_bit_alu_3_c_out), .R(R[3]), .C_Out(C_Out));
endmodule

module ALU16 (
  input  [3:0] ALU_Ctrl,
  input  C_In,
  input  [15:0] A,
  input  [15:0] B,
  output [15:0] R,
  output C_Out
);

  wire alu4_1_c_out, alu4_2_c_out, alu4_3_c_out;

  ALU4 alu4_1 (.ALU_Ctrl(ALU_Ctrl), .C_In(C_In), .A(A[3:0]), .B(B[3:0]), .R(R[3:0]), .C_Out(alu4_1_c_out));
  ALU4 alu4_2 (.ALU_Ctrl(ALU_Ctrl), .C_In(alu4_1_c_out), .A(A[7:4]), .B(B[7:4]), .R(R[7:4]), .C_Out(alu4_2_c_out));
  ALU4 alu4_3 (.ALU_Ctrl(ALU_Ctrl), .C_In(alu4_2_c_out), .A(A[11:8]), .B(B[11:8]), .R(R[11:8]), .C_Out(alu4_3_c_out));
  ALU4 alu4_4 (.ALU_Ctrl(ALU_Ctrl), .C_In(alu4_3_c_out), .A(A[15:12]), .B(B[15:12]), .R(R[15:12]), .C_Out(C_Out));
endmodule

module ALU32 (
  input  [3:0] ALU_Ctrl,
  input  C_In,
  input  [31:0] A,
  input  [31:0] B,
  output [31:0] R,
  output C_Out
);

  wire alu16_1_c_out;

  ALU16 alu16_1 (.ALU_Ctrl(ALU_Ctrl), .C_In(C_In), .A(A[15:0]), .B(B[15:0]), .R(R[15:0]), .C_Out(alu16_1_c_out));
  ALU16 alu16_2 (.ALU_Ctrl(ALU_Ctrl), .C_In(alu16_1_c_out), .A(A[31:16]), .B(B[31:16]), .R(R[31:16]), .C_Out(C_Out));
endmodule

module ALU_Control (
  input  I30,
  input  I14,
  input  I13,
  input  I12,
  input  I6,
  input  I5,
  input  I4,
  output ALU_Ctrl3,
  output ALU_Ctrl2,
  output ALU_Ctrl1,
  output ALU_Ctrl0,
  output ALU_Src
);

  wire and_2_out, not_1_out, not_2_out, not_3_out, not_4_out, not_5_out;

  not not_1 (not_1_out, I14);
  not not_2 (not_2_out, I13);
  not not_3 (not_3_out, I12);
  not not_4 (not_4_out, I5);
  not not_5 (not_5_out, I4);
  and and_1 (ALU_Ctrl2, I30, not_2_out, I5);
  or or_1 (ALU_Ctrl1, not_2_out, not_5_out);
  and and_2 (and_2_out, I13, not_3_out);
  or or_2 (ALU_Src, not_4_out, not_5_out);
  or or_3 (ALU_Ctrl0, not_1_out, and_2_out);

  assign ALU_Ctrl3 = 1'b0;
endmodule

module Reg_File_4_32_Zero (
  input  [1:0] RReg1,
  input  [1:0] RReg2,
  input  [31:0] WData,
  input  Clock_In,
  input  Write,
  input  [1:0] WReg,
  output [31:0] RData1,
  output [31:0] RData2
);

  wire demultiplexer_1_out0, demultiplexer_1_out1, demultiplexer_1_out2, demultiplexer_1_out3;
  wire [31:0] register_1_q, register_2_q, register_3_q, register_4_q;

  Demultiplexer #(.enable("false"), .select(2)) demultiplexer_1 (
    .out0(demultiplexer_1_out0), .out1(demultiplexer_1_out1), .out2(demultiplexer_1_out2),
    .out3(demultiplexer_1_out3), .in(Write), .sel(WReg));
  Register #(.width(32)) register_1 (
    .D(WData), .en(demultiplexer_1_out0), .clk(Clock_In), .Q(register_1_q), .clr(Write));
  Register #(.width(32)) register_2 (
    .D(WData), .en(demultiplexer_1_out1), .clk(Clock_In), .Q(register_2_q));  // open: clr
  Register #(.width(32)) register_3 (
    .D(WData), .en(demultiplexer_1_out2), .clk(Clock_In), .Q(register_3_q));  // open: clr
  Register #(.width(32)) register_4 (
    .D(WData), .en(demultiplexer_1_out3), .clk(Clock_In), .Q(register_4_q));  // open: clr
  Multiplexer #(.enable("false"), .select(2), .width(32)) multiplexer_1 (
    .in0(register_1_q), .in1(register_2_q), .in2(register_3_q), .in3(register_4_q), .out(RData1), .sel(RReg1));
  Multiplexer #(.enable("false"), .select(2), .width(32)) multiplexer_2 (
    .in0(register_1_q), .in1(register_2_q), .in2(register_3_q), .in3(register_4_q), .out(RData2), .sel(RReg2));
endmodule

module Register_File (
  input  [4:0] RReg1,
  input  [4:0] RReg2,
  input  Clock_In,
  input  [31:0] WData,
  input  Write,
  input  [4:0] WReg,
  output [31:0] RData1,
  output [31:0] RData2
);

  wire W3_0, W7_4, W11_8, W15_12, W19_16, W23_20, W27_24, W31_28;
  wire [31:0] reg_file_4_32_non_zero_1_rdata1, reg_file_4_32_non_zero_1_rdata2,
       reg_file_4_32_non_zero_2_rdata1, reg_file_4_32_non_zero_2_rdata2, reg_file_4_32_non_zero_3_rdata1,
       reg_file_4_32_non_zero_3_rdata2, reg_file_4_32_non_zero_4_rdata1, reg_file_4_32_non_zero_4_rdata2,
       reg_file_4_32_non_zero_5_rdata1, reg_file_4_32_non_zero_5_rdata2, reg_file_4_32_non_zero_6_rdata1,
       reg_file_4_32_non_zero_6_rdata2, reg_file_4_32_non_zero_7_rdata1, reg_file_4_32_non_zero_7_rdata2,
       reg_file_4_32_zero_1_rdata1, reg_file_4_32_zero_1_rdata2;

  Demultiplexer #(.enable("false"), .select(3)) demultiplexer_1 (
    .out0(W3_0), .out1(W7_4), .out2(W11_8), .out3(W15_12), .out4(W19_16), .out5(W23_20), .out6(W27_24),
    .out7(W31_28), .in(Write), .sel(WReg[4:2]));
  Reg_File_4_32_Zero reg_file_4_32_zero_1 (
    .RReg1(RReg1[1:0]), .RReg2(RReg2[1:0]), .WData(WData), .Clock_In(Clock_In), .Write(W3_0),
    .WReg(WReg[1:0]), .RData1(reg_file_4_32_zero_1_rdata1), .RData2(reg_file_4_32_zero_1_rdata2));
  Reg_File_4_32_Non_Zero reg_file_4_32_non_zero_1 (
    .RReg1(RReg1[1:0]), .RReg2(RReg2[1:0]), .WData(WData), .Clock_In(Clock_In), .Write(W7_4),
    .WReg(WReg[1:0]), .RData1(reg_file_4_32_non_zero_1_rdata1), .RData2(reg_file_4_32_non_zero_1_rdata2));
  Reg_File_4_32_Non_Zero reg_file_4_32_non_zero_2 (
    .RReg1(RReg1[1:0]), .RReg2(RReg2[1:0]), .WData(WData), .Clock_In(Clock_In), .Write(W11_8),
    .WReg(WReg[1:0]), .RData1(reg_file_4_32_non_zero_2_rdata1), .RData2(reg_file_4_32_non_zero_2_rdata2));
  Reg_File_4_32_Non_Zero reg_file_4_32_non_zero_3 (
    .RReg1(RReg1[1:0]), .RReg2(RReg2[1:0]), .WData(WData), .Clock_In(Clock_In), .Write(W15_12),
    .WReg(WReg[1:0]), .RData1(reg_file_4_32_non_zero_3_rdata1), .RData2(reg_file_4_32_non_zero_3_rdata2));
  Reg_File_4_32_Non_Zero reg_file_4_32_non_zero_4 (
    .RReg1(RReg1[1:0]), .RReg2(RReg2[1:0]), .WData(WData), .Clock_In(Clock_In), .Write(W19_16),
    .WReg(WReg[1:0]), .RData1(reg_file_4_32_non_zero_4_rdata1), .RData2(reg_file_4_32_non_zero_4_rdata2));
  Reg_File_4_32_Non_Zero reg_file_4_32_non_zero_5 (
    .RReg1(RReg1[1:0]), .RReg2(RReg2[1:0]), .WData(WData), .Clock_In(Clock_In), .Write(W23_20),
    .WReg(WReg[1:0]), .RData1(reg_file_4_32_non_zero_5_rdata1), .RData2(reg_file_4_32_non_zero_5_rdata2));
  Reg_File_4_32_Non_Zero reg_file_4_32_non_zero_6 (
    .RReg1(RReg1[1:0]), .RReg2(RReg2[1:0]), .WData(WData), .Clock_In(Clock_In), .Write(W27_24),
    .WReg(WReg[1:0]), .RData1(reg_file_4_32_non_zero_6_rdata1), .RData2(reg_file_4_32_non_zero_6_rdata2));
  Reg_File_4_32_Non_Zero reg_file_4_32_non_zero_7 (
    .RReg1(RReg1[1:0]), .RReg2(RReg2[1:0]), .WData(WData), .Clock_In(Clock_In), .Write(W31_28),
    .WReg(WReg[1:0]), .RData1(reg_file_4_32_non_zero_7_rdata1), .RData2(reg_file_4_32_non_zero_7_rdata2));
  Multiplexer #(.enable("false"), .select(3), .width(32)) multiplexer_1 (
    .in0(reg_file_4_32_zero_1_rdata1), .in1(reg_file_4_32_non_zero_1_rdata1),
    .in2(reg_file_4_32_non_zero_2_rdata1), .in3(reg_file_4_32_non_zero_3_rdata1),
    .in4(reg_file_4_32_non_zero_4_rdata1), .in5(reg_file_4_32_non_zero_5_rdata1),
    .in6(reg_file_4_32_non_zero_6_rdata1), .in7(reg_file_4_32_non_zero_7_rdata1), .out(RData1),
    .sel(RReg1[4:2]));
  Multiplexer #(.enable("false"), .select(3), .width(32)) multiplexer_2 (
    .in0(reg_file_4_32_zero_1_rdata2), .in1(reg_file_4_32_non_zero_1_rdata2),
    .in2(reg_file_4_32_non_zero_2_rdata2), .in3(reg_file_4_32_non_zero_3_rdata2),
    .in4(reg_file_4_32_non_zero_4_rdata2), .in5(reg_file_4_32_non_zero_5_rdata2),
    .in6(reg_file_4_32_non_zero_6_rdata2), .in7(reg_file_4_32_non_zero_7_rdata2), .out(RData2),
    .sel(RReg2[4:2]));
endmodule

module Reg_File_4_32_Non_Zero (
  input  [1:0] RReg1,
  input  [1:0] RReg2,
  input  [31:0] WData,
  input  Clock_In,
  input  Write,
  input  [1:0] WReg,
  output [31:0] RData1,
  output [31:0] RData2
);

  wire demultiplexer_1_out0, demultiplexer_1_out1, demultiplexer_1_out2, demultiplexer_1_out3;
  wire [31:0] register_1_q, register_2_q, register_3_q, register_4_q;

  Demultiplexer #(.enable("false"), .select(2)) demultiplexer_1 (
    .out0(demultiplexer_1_out0), .out1(demultiplexer_1_out1), .out2(demultiplexer_1_out2),
    .out3(demultiplexer_1_out3), .in(Write), .sel(WReg));
  Register #(.width(32)) register_1 (
    .D(WData), .en(demultiplexer_1_out0), .clk(Clock_In), .Q(register_1_q));  // open: clr
  Register #(.width(32)) register_2 (
    .D(WData), .en(demultiplexer_1_out1), .clk(Clock_In), .Q(register_2_q));  // open: clr
  Register #(.width(32)) register_3 (
    .D(WData), .en(demultiplexer_1_out2), .clk(Clock_In), .Q(register_3_q));  // open: clr
  Register #(.width(32)) register_4 (
    .D(WData), .en(demultiplexer_1_out3), .clk(Clock_In), .Q(register_4_q));  // open: clr
  Multiplexer #(.enable("false"), .select(2), .width(32)) multiplexer_1 (
    .in0(register_1_q), .in1(register_2_q), .in2(register_3_q), .in3(register_4_q), .out(RData1), .sel(RReg1));
  Multiplexer #(.enable("false"), .select(2), .width(32)) multiplexer_2 (
    .in0(register_1_q), .in1(register_2_q), .in2(register_3_q), .in3(register_4_q), .out(RData2), .sel(RReg2));
endmodule

module Datapath (
  input  C_In,
  input  [31:0] Instruction,
  output C_Out
);

  wire alu_control_1_alu_src, clock_1_out;
  wire [3:0] alu_control_1_alu_ctrl0;
  wire [31:0] alu32_1_r, bit_extender_1_out, multiplexer_1_out, register_file_1_rdata1,
       register_file_1_rdata2;

  Clock clock_1 (.out(clock_1_out));
  assign bit_extender_1_out = {{20{Instruction[31]}}, Instruction[31:20]};  // Bit_Extender bit_extender_1
  Register_File register_file_1 (
    .RReg1(Instruction[19:15]), .RReg2(Instruction[24:20]), .Clock_In(clock_1_out), .WData(alu32_1_r),
    .Write(1'b1), .WReg(Instruction[11:7]), .RData1(register_file_1_rdata1), .RData2(register_file_1_rdata2));
  ALU_Control alu_control_1 (
    .I30(Instruction[30]), .I14(Instruction[14]), .I13(Instruction[13]), .I12(Instruction[12]),
    .I6(Instruction[6]), .I5(Instruction[5]), .I4(Instruction[4]), .ALU_Ctrl3(alu_control_1_alu_ctrl0[3]),
    .ALU_Ctrl2(alu_control_1_alu_ctrl0[2]), .ALU_Ctrl1(alu_control_1_alu_ctrl0[1]),
    .ALU_Ctrl0(alu_control_1_alu_ctrl0[0]), .ALU_Src(alu_control_1_alu_src));
  Multiplexer #(.enable("false"), .width(32)) multiplexer_1 (
    .in0(register_file_1_rdata2), .in1(bit_extender_1_out), .out(multiplexer_1_out),
    .sel(alu_control_1_alu_src));
  ALU32 alu32_1 (
    .ALU_Ctrl(alu_control_1_alu_ctrl0), .C_In(C_In), .A(register_file_1_rdata1), .B(multiplexer_1_out),
    .R(alu32_1_r), .C_Out(C_Out));
endmodule
